// Logisim project Project1.circ as structural Verilog
module NAND (
  input  in_1,
  input  in_2,
  output out_3
);

  wire and_1_out;

  not not_1 (out_3, and_1_out);
  and and_1 (and_1_out, in_1, in_2);
endmodule

module AND (
  input  in_1,
  input  in_2,
  output out_3
);

  wire nand_1_out_3, nand_2_out_3;

  NAND nand_1 (.in_1(in_1), .in_2(in_2), .out_3(nand_1_out_3));
  NAND nand_2 (.in_1(in_1), .in_2(in_2), .out_3(nand_2_out_3));
  NAND nand_3 (.in_1(nand_1_out_3), .in_2(nand_2_out_3), .out_3(out_3));
endmodule

module OR (
  input  in_1,
  input  in_2,
  output out_3
);

  wire nand_1_out_3, nand_2_out_3;

  NAND nand_1 (.in_1(in_1), .in_2(in_1), .out_3(nand_1_out_3));
  NAND nand_2 (.in_1(in_2), .in_2(in_2), .out_3(nand_2_out_3));
  NAND nand_3 (.in_1(nand_1_out_3), .in_2(nand_2_out_3), .out_3(out_3));
endmodule

module NOT (
  input  in_1,
  output out_2
);

  NAND nand_1 (.in_1(in_1), .in_2(in_1), .out_3(out_2));
endmodule

module Truthtable (
  input  A,
  input  B,
  input  C,
  output X,
  output Y
);

  wire and_1_out, and_2_out, and_3_out, or_1_out, or_2_out, or_3_out;

  and and_1 (and_1_out, A, C);
  and and_2 (and_2_out, B, C);
  or or_1 (or_1_out, B, and_2_out);
  and and_3 (and_3_out, and_2_out, B);
  or or_2 (or_2_out, and_1_out, or_1_out);
  or or_3 (or_3_out, and_1_out, and_3_out);
  not not_1 (X, or_2_out);
  not not_2 (Y, or_3_out);
endmodule

module BinaryDisplay (
);

  _7_Segment_Display u_7_segment_display_1 ();  // open: g, f, a, b, e, d, c, dp
endmodule
